# Fritzing sketch drone (saved by Fritzing 0.9.3b)
circuit board: 8.46667cm x 5.64444cm
perfboards: 1

parts:
  D4 = Rectifier Diode [part_number=1N4001 package="300 mil [THT]"]
  M4 = DC Motor
  C1 = Ceramic Capacitor [capacitance=100nF package="100 mil [THT, multilayer]"]
  R3 = Resistor [tolerance=±5% resistance=1k package=THT]
  Arduino_PLC = Arduino Pro Mini v13
  M2 = DC Motor
  R2 = Resistor [tolerance=±5% resistance=1k package=THT]
  D1 = Rectifier Diode [part_number=1N4001 package="300 mil [THT]"]
  R1 = Resistor [tolerance=±5% resistance=1k package=THT]
  R4 = Resistor [tolerance=±5% resistance=1k package=THT]
  Q3 = MOSFET-NCHANNEL [package=to-92]
  D3 = Rectifier Diode [part_number=1N4001 package="300 mil [THT]"]
  Q2 = MOSFET-NCHANNEL [package=to-92]
  C2 = Ceramic Capacitor [capacitance=100nF package="100 mil [THT, multilayer]"]
  M1 = DC Motor
  Lipo_600_mAh = Battery Holders [package=lipo-1100mAh]
  Q5 = MOSFET-NCHANNEL [package=to-92]
  M3 = DC Motor
  D2 = Rectifier Diode [part_number=1N4001 package="300 mil [THT]"]
  3_7v-5v_regulator = IC, DIP package, 4 pins [chip_label=3.7v-5v]
  5V-3_3V_regulator = IC, DIP package, 4 pins [chip_label=5V-3.3V]
  MPU-6050 = InvenSense MPU6050
  元件1 = NRF24L01+ Breakout Board
  Q4 = MOSFET-NCHANNEL [package=to-92]

nets:
  N1: D4.cathode, M4.pin_1, C1.0, M2.pin_1, D1.cathode, D3.cathode, C2.0, M1.pin_1, Lipo_600_mAh.+, M3.pin_1, D2.cathode, 3_7v-5v_regulator.pin3
  N2: D4.anode, Q2.D, M1.pin_2
  N3: M4.pin_2, Q5.D, D2.anode
  N4: C1.1, R3.Pin_1, R2.Pin_1, R1.Pin_1, R4.Pin_1, Q3.S, Q2.S, C2.1, Lipo_600_mAh.-, Q5.S, 3_7v-5v_regulator.pin4, Q4.S
  N5: R3.Pin_0, Arduino_PLC.D6_PWM, Q4.G
  N6: Arduino_PLC.VCC, 5V-3_3V_regulator.pin4
  N7: Arduino_PLC.GND, 3_7v-5v_regulator.pin1, 5V-3_3V_regulator.pin3
  N8: Arduino_PLC.A4, MPU-6050.SCL
  N9: Arduino_PLC.A5, MPU-6050.SDA
  N10: Arduino_PLC.RAW, 3_7v-5v_regulator.pin2
  N11: Arduino_PLC.D13/SCK, 元件1.SCK
  N12: Arduino_PLC.D12/MISO, 元件1.MISO
  N13: Arduino_PLC.D11_PWM/MOSI, 元件1.MOSI
  N14: Arduino_PLC.D9_PWM, R4.Pin_0, Q5.G
  N15: Arduino_PLC.D8, 元件1.CS
  N16: Arduino_PLC.D7, 元件1.CE
  N17: Arduino_PLC.D5_PWM, R2.Pin_0, Q3.G
  N18: Arduino_PLC.D3_PWM, R1.Pin_0, Q2.G
  N19: M2.pin_2, Q3.D, D3.anode
  N20: D1.anode, M3.pin_2, Q4.D
  VCC: 5V-3_3V_regulator.pin1, MPU-6050.VCC, 元件1.VCC
  GND: 5V-3_3V_regulator.pin2, MPU-6050.GND, 元件1.GND
