# Fritzing sketch drone_arduino_modules (saved by Fritzing 0.9.3b)
circuit board: 8.46667cm x 5.64444cm
perfboards: 1

parts:
  Arduino_PLC = Arduino Pro Mini v13
  3_7v-5v_regulator = IC, DIP package, 4 pins [chip_label=3.7v-5v]
  5V-3_3V_regulator = IC, DIP package, 4 pins [chip_label=5V-3.3V]
  MPU-6050 = InvenSense MPU6050
  元件1 = NRF24L01+ Breakout Board
  J1 = female pin header, 4 pins [form="♀ (female)"]
  R1 = Resistor [tolerance=±5% resistance=220 package=THT]
  R2 = Resistor [tolerance=±5% resistance=220 package=THT]
  R3 = Resistor [tolerance=±5% resistance=220 package=THT]
  R4 = Resistor [tolerance=±5% resistance=220 package=THT]

nets:
  N1: Arduino_PLC.VCC, 5V-3_3V_regulator.pin4
  N2: Arduino_PLC.GND, 3_7v-5v_regulator.pin1, 5V-3_3V_regulator.pin3
  N3: Arduino_PLC.A4, MPU-6050.SCL
  N4: Arduino_PLC.A5, MPU-6050.SDA
  N5: Arduino_PLC.RAW, 3_7v-5v_regulator.pin2
  N6: Arduino_PLC.D13/SCK, 元件1.SCK
  N7: Arduino_PLC.D12/MISO, 元件1.MISO
  N8: Arduino_PLC.D11_PWM/MOSI, 元件1.MOSI
  N9: Arduino_PLC.D9_PWM, R1.Pin_0
  N10: Arduino_PLC.D8, 元件1.CS
  N11: Arduino_PLC.D7, 元件1.CE
  N12: Arduino_PLC.D6_PWM, R2.Pin_0
  N13: Arduino_PLC.D5_PWM, R3.Pin_0
  N14: Arduino_PLC.D3_PWM, R4.Pin_0
  N15: Arduino_PLC.D2, MPU-6050.INT
  VCC: 5V-3_3V_regulator.pin1, MPU-6050.VCC, 元件1.VCC
  GND: 5V-3_3V_regulator.pin2, MPU-6050.GND, 元件1.GND
  N16: J1.pin1, R4.Pin_1
  N17: J1.pin2, R3.Pin_1
  N18: J1.pin3, R2.Pin_1
  N19: J1.pin4, R1.Pin_1

notes:
  Interrupt Pin!! and resistor - change on the main.
  Change resistor location.
  Front choice 2(difficult for power?) X-R, Y-P, Z-Y. Currently chosen
  Left to right: 1-4 from front choice 2.
  Front choice 1 X-P, Y-R, Z-Y.
