# Fritzing sketch drone_motor_driver (saved by Fritzing 0.9.3b)
circuit board: 3cm x 3.5cm
perfboards: 1

parts:
  D4 = Rectifier Diode [part_number=1N4001 package="300 mil [THT]"]
  R1 = Resistor [tolerance=±5% resistance=1k package=THT]
  M1 = DC Motor
  J1 = female pin header, 1 pin [form="♀ (female)"]
  R2 = Resistor [tolerance=±5% resistance=1k package=THT]
  M2 = DC Motor
  D5 = Rectifier Diode [part_number=1N4001 package="300 mil [THT]"]
  J2 = female pin header, 1 pin [form="♀ (female)"]
  R3 = Resistor [tolerance=±5% resistance=1k package=THT]
  M3 = DC Motor
  D6 = Rectifier Diode [part_number=1N4001 package="300 mil [THT]"]
  J3 = female pin header, 1 pin [form="♀ (female)"]
  R4 = Resistor [tolerance=±5% resistance=1k package=THT]
  M4 = DC Motor
  D7 = Rectifier Diode [part_number=1N4001 package="300 mil [THT]"]
  J4 = female pin header, 1 pin [form="♀ (female)"]
  Q6 = MOSFET-NCHANNEL [package=to-92]
  Q7 = MOSFET-NCHANNEL [package=to-92]
  Q8 = MOSFET-NCHANNEL [package=to-92]
  Q9 = MOSFET-NCHANNEL [package=to-92]
  C1 = Electrolytic Capacitor [capacitance=0.1mF package="100 mil [THT, electrolytic]"]
  C2 = Electrolytic Capacitor [capacitance=0.1mF package="100 mil [THT, electrolytic]"]

nets:
  3.7V: D4.cathode, M1.pin_1, M2.pin_1, D5.cathode, M3.pin_1, D6.cathode, M4.pin_1, D7.cathode, C1.+, C2.+
  N1: D4.anode, M1.pin_2, Q8.D
  N2: R1.Pin_0, J1.pin1, Q8.G
  GND: R1.Pin_1, R2.Pin_1, R3.Pin_1, R4.Pin_1, Q6.S, Q7.S, Q8.S, Q9.S, C1.-, C2.-
  N3: R2.Pin_0, J2.pin1, Q9.G
  N4: M2.pin_2, D5.anode, Q9.D
  N5: R3.Pin_0, J3.pin1, Q7.G
  N6: M3.pin_2, D6.anode, Q7.D
  N7: R4.Pin_0, J4.pin1, Q6.G
  N8: M4.pin_2, D7.anode, Q6.D

notes:
  red/black first, yellow last? NO, the order of soldering is not determined yet.
  CCW 1 to 4 from left top(from front perspective). This is back
  All power should go directly to the source

custom parts:
  MOSFET-NCHANNEL: Generic NMOS footprint
